// Logisim project T3.circ as structural Verilog: 1 circuit, main circuit main
module main (
  input  A,
  input  C,
  input  B,
  input  D,
  output F
);

  wire nor_1_out, nor_2_out, nor_3_out, nor_4_out, not_1_out, not_2_out, not_3_out, not_4_out;

  not not_1 (not_1_out, A);
  not not_2 (not_2_out, C);
  not not_3 (not_3_out, B);
  not not_4 (not_4_out, D);
  nor nor_1 (nor_1_out, C, not_1_out);
  nor nor_2 (nor_2_out, A, not_2_out);
  nor nor_3 (nor_3_out, not_3_out, D);
  nor nor_4 (nor_4_out, not_4_out, B);
  nor nor_5 (F, nor_1_out, nor_4_out);
endmodule
