// Logisim project T2比较器.circ as structural Verilog: 1 circuit, main circuit main
module main (
  input  A,
  input  B,
  output F1,
  output F2,
  output F3
);

  wire and_2_out, and_3_out, not_1_out, not_2_out;

  not not_1 (not_1_out, A);
  not not_2 (not_2_out, B);
  and and_1 (F1, A, not_2_out);
  and and_2 (and_2_out, not_1_out, not_2_out);
  and and_3 (and_3_out, A, B);
  and and_4 (F3, not_1_out, B);
  or or_1 (F2, and_2_out, and_3_out);

  // Notes on the sheet:
  //   A: initial=0x1
endmodule
