// Logisim project T4.circ as structural Verilog: 1 circuit, main circuit main
module main (
  input  X,
  input  A,
  input  B,
  input  Ci,
  output Co,
  output Y
);

  wire and_1_out, and_2_out, and_3_out, and_4_out, and_5_out, and_6_out, and_7_out, and_8_out, and_9_out,
       not_1_out, not_2_out, not_3_out, not_4_out;

  not not_1 (not_1_out, X);
  not not_2 (not_2_out, A);
  not not_3 (not_3_out, B);
  not not_4 (not_4_out, Ci);
  and and_1 (and_1_out, B, X, not_2_out);
  and and_2 (and_2_out, Ci, not_2_out, X);
  and and_3 (and_3_out, A, B, not_1_out);
  and and_4 (and_4_out, A, Ci, not_1_out);
  and and_5 (and_5_out, Ci, B);
  and and_6 (and_6_out, B, not_2_out, not_4_out);
  and and_7 (and_7_out, not_2_out, not_3_out, Ci);
  and and_8 (and_8_out, not_3_out, not_4_out, A);
  and and_9 (and_9_out, Ci, B, A);
  or or_1 (Co, and_1_out, and_2_out, and_3_out, and_4_out, and_5_out);
  or or_2 (Y, and_6_out, and_7_out, and_8_out, and_9_out);
endmodule
