// Logisim project T5.circ as structural Verilog: 1 circuit, main circuit main
module main (
  input  A,
  input  B,
  input  C,
  input  D,
  output W,
  output X,
  output Y,
  output Z
);

  wire and_1_out, and_2_out, and_3_out, and_4_out, and_5_out, not_1_out, not_2_out, not_3_out;

  not not_1 (not_1_out, D);
  not not_2 (not_2_out, B);
  not not_3 (not_3_out, C);
  and and_1 (and_1_out, D, B);
  and and_2 (and_2_out, C, B);
  and and_3 (and_3_out, not_1_out, B);
  and and_4 (and_4_out, not_2_out, C);
  and and_5 (and_5_out, not_3_out, B, D);
  or or_1 (W, A, and_1_out, and_2_out);
  or or_2 (X, A, and_2_out, and_3_out);
  or or_3 (Y, A, and_4_out, and_5_out);

  assign Z = D;
endmodule
