// Logisim project T6_2.circ as structural Verilog: 1 circuit, main circuit main
module main (
  input  D,
  input  B,
  input  C,
  input  A,
  output F
);

  wire n7485_1_pin1, n7485_1_pin3, n7485_1_pin6, nand_1_out, nor_1_out, not_1_out;

  not not_1 (not_1_out, D);
  nor nor_1 (nor_1_out, A, B);
  nand nand_1 (nand_1_out, C, not_1_out);
  _7485 #(.ShowInternalStructure("true")) u_7485_1 (
    .pin1(n7485_1_pin1), .pin2(n7485_1_pin1), .pin3(n7485_1_pin3), .pin4(n7485_1_pin1), .pin6(n7485_1_pin6),
    .pin15(n7485_1_pin1), .pin14(n7485_1_pin1), .pin13(n7485_1_pin1), .pin12(A), .pin11(C), .pin10(B),
    .pin9(D));  // open: pin5, pin7
  or or_1 (F, nor_1_out, nand_1_out, n7485_1_pin6);
  // also tied to GND on the sheet: n7485_1_pin1
  // also tied to VCC on the sheet: n7485_1_pin3
endmodule
